// Digital circuit ALU.dig as structural Verilog
module ALU (
  input  BIT_1,
  input  BIT_2,
  input  BIT_3,
  input  BIT_4,
  input  BIT_5,
  input  BIT_6,
  input  BIT_7,
  input  BIT_8,
  input  BIT_1_2,
  input  BIT_2_2,
  input  BIT_3_2,
  input  BIT_4_2,
  input  BIT_5_2,
  input  BIT_6_2,
  input  BIT_7_2,
  input  BIT_8_2,
  input  Add___Subtract,
  output SUM_1,
  output SUM_2,
  output SUM_3,
  output SUM_4,
  output SUM_5,
  output SUM_6,
  output SUM_7,
  output SUM_8
);

  wire driver_1_out, driver_2_out, not_1_out, or_1_out, or_2_out, S_1_c_o, S_2_c_o, S_3_c_o, S_4_c_o,
       S_5_c_o, S_6_c_o, S_7_c_o, S_8_c_o, xor_1_out, xor_2_out, xor_3_out, xor_4_out, xor_5_out, xor_6_out,
       xor_7_out, xor_8_out;

  Add S_1 (.a(BIT_1), .b(xor_1_out), .c_i(S_2_c_o), .s(SUM_1), .c_o(S_1_c_o));
  Add S_2 (.a(BIT_2), .b(xor_2_out), .c_i(S_3_c_o), .s(SUM_2), .c_o(S_2_c_o));
  not not_1 (not_1_out, or_1_out);
  assign driver_1_out = not_1_out ? not_1_out : 1'bz;  // Driver driver_1
  Add S_3 (.a(BIT_3), .b(xor_3_out), .c_i(S_4_c_o), .s(SUM_3), .c_o(S_3_c_o));
  or or_1 (or_1_out, SUM_8, SUM_7, SUM_6, SUM_5, SUM_4, SUM_3, SUM_2, SUM_1);
  Add S_4 (.a(BIT_4), .b(xor_4_out), .c_i(S_5_c_o), .s(SUM_4), .c_o(S_4_c_o));
  Add S_5 (.a(BIT_5), .b(xor_5_out), .c_i(S_6_c_o), .s(SUM_5), .c_o(S_5_c_o));
  Add S_6 (.a(BIT_6), .b(xor_6_out), .c_i(S_7_c_o), .s(SUM_6), .c_o(S_6_c_o));
  Add S_7 (.a(BIT_7), .b(xor_7_out), .c_i(S_8_c_o), .s(SUM_7), .c_o(S_7_c_o));
  Add S_8 (.a(BIT_8), .b(xor_8_out), .c_i(Add___Subtract), .s(SUM_8), .c_o(S_8_c_o));
  or or_2 (or_2_out, S_1_c_o, 1'b0);
  assign driver_2_out = or_2_out ? or_2_out : 1'bz;  // Driver driver_2
  xor xor_1 (xor_1_out, BIT_1_2, Add___Subtract);
  xor xor_2 (xor_2_out, BIT_2_2, Add___Subtract);
  xor xor_3 (xor_3_out, BIT_3_2, Add___Subtract);
  xor xor_4 (xor_4_out, BIT_4_2, Add___Subtract);
  xor xor_5 (xor_5_out, BIT_5_2, Add___Subtract);
  xor xor_6 (xor_6_out, BIT_6_2, Add___Subtract);
  xor xor_7 (xor_7_out, BIT_7_2, Add___Subtract);
  xor xor_8 (xor_8_out, BIT_8_2, Add___Subtract);
endmodule
