// Digital circuit Control_unit_(CU).dig as structural Verilog
module Control_unit__CU (
  input  in_1,
  input  in_2,
  input  in_3,
  input  in_4,
  input  in_5,
  input  in_6,
  input  in_7,
  input  Carry_flag,
  input  Zero_flag
);

  wire and_1_out, and_2_out, and_3_out, and_4_out, and_7_out, and_8_out, and_10_out, and_11_out, and_12_out,
       and_13_out, and_14_out, and_15_out, and_16_out, and_17_out, and_18_out, and_19_out, and_20_out,
       and_21_out, and_22_out, and_23_out, and_24_out, and_25_out, and_26_out, and_27_out, and_28_out,
       and_29_out, and_30_out, and_31_out, and_32_out, and_33_out, and_34_out, and_35_out, and_36_out,
       and_37_out, and_38_out, and_39_out, and_40_out, and_41_out, not_1_out, not_2_out, not_3_out,
       not_4_out, not_5_out, not_6_out, not_7_out, not_8_out, not_9_out, or_1_out, or_2_out, or_3_out,
       or_4_out, or_5_out, or_6_out, or_7_out, or_8_out, or_9_out, or_10_out;

  not not_1 (not_1_out, Carry_flag);
  not not_2 (not_2_out, Zero_flag);
  and and_1 (and_1_out, not_1_out, not_2_out);
  and and_2 (and_2_out, not_1_out, Zero_flag);
  and and_3 (and_3_out, Carry_flag, not_2_out);
  and and_4 (and_4_out, Carry_flag, Zero_flag);
  not not_3 (not_3_out, in_1);
  not not_4 (not_4_out, in_2);
  not not_5 (not_5_out, in_3);
  // And and_5 has open pins: In_1=not_3_out, In_2=not_4_out, In_3=not_5_out, out=open
  // And and_6 has open pins: In_1=not_3_out, In_2=not_4_out, In_3=in_3, out=open
  and and_7 (and_7_out, not_3_out, in_2, not_5_out);
  and and_8 (and_8_out, not_3_out, in_2, in_3);
  // And and_9 has open pins: In_1=in_1, In_2=not_4_out, In_3=not_5_out, out=open
  not not_6 (not_6_out, in_4);
  not not_7 (not_7_out, in_5);
  not not_8 (not_8_out, in_6);
  not not_9 (not_9_out, in_7);
  and and_10 (and_10_out, not_6_out, not_7_out, not_8_out, not_9_out);
  and and_11 (and_11_out, not_6_out, not_7_out, not_8_out, in_7);
  and and_12 (and_12_out, not_6_out, not_7_out, in_6, not_9_out);
  and and_13 (and_13_out, not_6_out, not_7_out, in_6, in_7);
  and and_14 (and_14_out, not_6_out, in_5, not_8_out, not_9_out);
  and and_15 (and_15_out, not_6_out, in_5, not_8_out, in_7);
  and and_16 (and_16_out, not_6_out, in_5, in_6, not_9_out);
  and and_17 (and_17_out, not_6_out, in_5, in_6, in_7);
  and and_18 (and_18_out, in_4, not_7_out, not_8_out, not_9_out);
  and and_19 (and_19_out, in_4, not_7_out, not_8_out, in_7);
  and and_20 (and_20_out, and_10_out, and_7_out);
  and and_21 (and_21_out, and_10_out, and_8_out);
  and and_22 (and_22_out, and_11_out, and_7_out);
  and and_23 (and_23_out, and_12_out, and_7_out);
  and and_24 (and_24_out, and_12_out, and_8_out);
  and and_25 (and_25_out, and_13_out, and_7_out);
  and and_26 (and_26_out, and_13_out, and_8_out);
  and and_27 (and_27_out, and_14_out, and_7_out);
  and and_28 (and_28_out, and_14_out, and_8_out);
  and and_29 (and_29_out, and_15_out, and_7_out);
  and and_30 (and_30_out, and_16_out, and_7_out);
  and and_31 (and_31_out, and_17_out, and_7_out);
  and and_32 (and_32_out, and_18_out, and_7_out);
  and and_33 (and_33_out, and_19_out, and_7_out);
  and and_34 (and_34_out, and_30_out, and_1_out);
  and and_35 (and_35_out, and_30_out, and_2_out);
  and and_36 (and_36_out, and_30_out, and_3_out);
  and and_37 (and_37_out, and_30_out, and_4_out);
  and and_38 (and_38_out, and_31_out, and_1_out);
  and and_39 (and_39_out, and_31_out, and_2_out);
  and and_40 (and_40_out, and_31_out, and_3_out);
  and and_41 (and_41_out, and_31_out, and_4_out);
  or or_1 (or_1_out, and_41_out, and_39_out, and_37_out, and_36_out, and_29_out, and_27_out, and_25_out, and_23_out, and_22_out, and_20_out);
  or or_2 (or_2_out, and_27_out, and_25_out, and_23_out, and_20_out);
  or or_3 (or_3_out, and_22_out, and_21_out);
  or or_4 (or_4_out, and_26_out, and_24_out, and_21_out);
  or or_5 (or_5_out, and_32_out, and_28_out);
  or or_6 (or_6_out, and_26_out, and_24_out);
  or or_7 (or_7_out, and_41_out, and_39_out, and_37_out, and_36_out, and_29_out);
  or or_8 (or_8_out, 1'b0, and_28_out);
  or or_9 (or_9_out, 1'b0, and_26_out);
  or or_10 (or_10_out, 1'b0, and_33_out);
endmodule
