// Digital circuit Display_register_(DR).dig as structural Verilog
module Display_register__DR (
  input  in_1,
  input  in_2,
  input  in_3,
  input  in_4,
  input  in_5,
  input  in_6,
  input  in_7,
  input  in_8,
  input  Display_OUT
);

  wire and_1_out, and_2_out, and_3_out, and_4_out, and_5_out, and_6_out, and_7_out, and_8_out, and_9_out,
       and_10_out, and_11_out, and_12_out, and_13_out, and_14_out, and_15_out, and_16_out, and_17_out,
       and_18_out, and_19_out, and_20_out, and_21_out, and_22_out, and_23_out, and_24_out, and_25_out,
       and_26_out, and_27_out, and_28_out, and_29_out, and_30_out, and_31_out, and_32_out, d_ff_1_q,
       d_ff_2_q, d_ff_3_q, d_ff_4_q, d_ff_5_q, d_ff_6_q, d_ff_7_q, d_ff_8_q, not_1_out, not_2_out, not_3_out,
       not_4_out, not_5_out, not_6_out, not_7_out, not_8_out, not_9_out, not_10_out, not_11_out, not_12_out,
       not_13_out, not_14_out, not_15_out, not_16_out, or_1_out, or_2_out, or_3_out, or_4_out, or_5_out,
       or_6_out, or_7_out, or_8_out, or_9_out, or_10_out, or_11_out, or_12_out, or_13_out;

  not not_1 (not_1_out, d_ff_1_q);
  not not_2 (not_2_out, d_ff_2_q);
  not not_3 (not_3_out, d_ff_3_q);
  not not_4 (not_4_out, d_ff_4_q);
  not not_5 (not_5_out, d_ff_5_q);
  not not_6 (not_6_out, d_ff_6_q);
  not not_7 (not_7_out, d_ff_7_q);
  not not_8 (not_8_out, d_ff_8_q);
  and and_1 (and_1_out, not_1_out, not_2_out, not_3_out, not_4_out, not_5_out, not_6_out, not_7_out, not_8_out);
  and and_2 (and_2_out, not_1_out, not_2_out, not_3_out, not_4_out, not_5_out, not_6_out, not_7_out, d_ff_8_q);
  and and_3 (and_3_out, not_1_out, not_2_out, not_3_out, not_4_out, not_5_out, not_6_out, d_ff_7_q, not_8_out);
  and and_4 (and_4_out, not_1_out, not_2_out, not_3_out, not_4_out, not_5_out, not_6_out, d_ff_7_q, d_ff_8_q);
  and and_5 (and_5_out, not_1_out, not_2_out, not_3_out, not_4_out, not_5_out, d_ff_6_q, not_7_out, not_8_out);
  and and_6 (and_6_out, not_1_out, not_2_out, not_3_out, not_4_out, not_5_out, d_ff_6_q, not_7_out, d_ff_8_q);
  and and_7 (and_7_out, not_1_out, not_2_out, not_3_out, not_4_out, not_5_out, d_ff_6_q, d_ff_7_q, not_8_out);
  and and_8 (and_8_out, not_1_out, not_2_out, not_3_out, not_4_out, not_5_out, d_ff_6_q, d_ff_7_q, d_ff_8_q);
  and and_9 (and_9_out, not_1_out, not_2_out, not_3_out, not_4_out, d_ff_5_q, not_6_out, not_7_out, not_8_out);
  and and_10 (and_10_out, not_1_out, not_2_out, not_3_out, not_4_out, d_ff_5_q, not_6_out, not_7_out, d_ff_8_q);
  and and_11 (and_11_out, not_1_out, not_2_out, not_3_out, not_4_out, d_ff_5_q, not_6_out, d_ff_7_q, not_8_out);
  and and_12 (and_12_out, not_1_out, not_2_out, not_3_out, not_4_out, d_ff_5_q, not_6_out, d_ff_7_q, d_ff_8_q);
  and and_13 (and_13_out, not_1_out, not_2_out, not_3_out, not_4_out, d_ff_5_q, d_ff_6_q, not_7_out, not_8_out);
  and and_14 (and_14_out, not_1_out, not_2_out, not_3_out, not_4_out, d_ff_5_q, d_ff_6_q, not_7_out, d_ff_8_q);
  and and_15 (and_15_out, not_1_out, not_2_out, not_3_out, not_4_out, d_ff_5_q, d_ff_6_q, d_ff_7_q, not_8_out);
  and and_16 (and_16_out, not_1_out, not_2_out, not_3_out, not_4_out, d_ff_5_q, d_ff_6_q, d_ff_7_q, d_ff_8_q);
  or or_1 (or_1_out, and_10_out, and_9_out, and_8_out, and_7_out, and_6_out, and_5_out, and_4_out, and_3_out, and_2_out, and_1_out);
  or or_2 (or_2_out, and_10_out, and_9_out, and_8_out, and_7_out, and_6_out, and_5_out, and_4_out, and_3_out, and_2_out, and_1_out);
  or or_3 (or_3_out, and_10_out, and_9_out, and_8_out, and_7_out, and_6_out, and_5_out, and_4_out, and_3_out, and_2_out, and_1_out);
  Seven_Seg seven_seg_1 (
    .a(or_1_out), .b(or_2_out), .c(or_3_out), .d(or_4_out), .e(or_5_out), .f(or_6_out), .g(1'b0), .dp(1'b0));
  or or_4 (or_4_out, and_10_out, and_9_out, and_8_out, and_7_out, and_6_out, and_5_out, and_4_out, and_3_out, and_2_out, and_1_out);
  or or_5 (or_5_out, and_16_out, and_15_out, and_14_out, and_13_out, and_12_out, and_11_out, and_10_out, and_9_out, and_8_out, and_7_out, and_6_out, and_5_out, and_4_out, and_3_out, and_2_out, and_1_out);
  or or_6 (or_6_out, and_16_out, and_15_out, and_14_out, and_13_out, and_12_out, and_11_out, and_10_out, and_9_out, and_8_out, and_7_out, and_6_out, and_5_out, and_4_out, and_3_out, and_2_out, and_1_out);
  D_FF d_ff_1 (.D(in_1), .C(Display_OUT), .Q(d_ff_1_q));  // open: nQ
  D_FF d_ff_2 (.D(in_2), .C(Display_OUT), .Q(d_ff_2_q));  // open: nQ
  not not_9 (not_9_out, d_ff_1_q);
  D_FF d_ff_3 (.D(in_3), .C(Display_OUT), .Q(d_ff_3_q));  // open: nQ
  D_FF d_ff_4 (.D(in_4), .C(Display_OUT), .Q(d_ff_4_q));  // open: nQ
  D_FF d_ff_5 (.D(in_5), .C(Display_OUT), .Q(d_ff_5_q));  // open: nQ
  not not_10 (not_10_out, d_ff_2_q);
  D_FF d_ff_6 (.D(in_6), .C(Display_OUT), .Q(d_ff_6_q));  // open: nQ
  not not_11 (not_11_out, d_ff_3_q);
  D_FF d_ff_7 (.D(in_7), .C(Display_OUT), .Q(d_ff_7_q));  // open: nQ
  not not_12 (not_12_out, d_ff_4_q);
  D_FF d_ff_8 (.D(in_8), .C(Display_OUT), .Q(d_ff_8_q));  // open: nQ
  not not_13 (not_13_out, d_ff_5_q);
  not not_14 (not_14_out, d_ff_6_q);
  not not_15 (not_15_out, d_ff_7_q);
  not not_16 (not_16_out, d_ff_8_q);
  and and_17 (and_17_out, not_9_out, not_10_out, not_11_out, not_12_out, not_13_out, not_14_out, not_15_out, not_16_out);
  and and_18 (and_18_out, not_9_out, not_10_out, not_11_out, not_12_out, not_13_out, not_14_out, not_15_out, d_ff_8_q);
  and and_19 (and_19_out, not_9_out, not_10_out, not_11_out, not_12_out, not_13_out, not_14_out, d_ff_7_q, not_16_out);
  and and_20 (and_20_out, not_9_out, not_10_out, not_11_out, not_12_out, not_13_out, not_14_out, d_ff_7_q, d_ff_8_q);
  and and_21 (and_21_out, not_9_out, not_10_out, not_11_out, not_12_out, not_13_out, d_ff_6_q, not_15_out, not_16_out);
  and and_22 (and_22_out, not_9_out, not_10_out, not_11_out, not_12_out, not_13_out, d_ff_6_q, not_15_out, d_ff_8_q);
  and and_23 (and_23_out, not_9_out, not_10_out, not_11_out, not_12_out, not_13_out, d_ff_6_q, d_ff_7_q, not_16_out);
  and and_24 (and_24_out, not_9_out, not_10_out, not_11_out, not_12_out, not_13_out, d_ff_6_q, d_ff_7_q, d_ff_8_q);
  and and_25 (and_25_out, not_9_out, not_10_out, not_11_out, not_12_out, d_ff_5_q, not_14_out, not_15_out, not_16_out);
  and and_26 (and_26_out, not_9_out, not_10_out, not_11_out, not_12_out, d_ff_5_q, not_14_out, not_15_out, d_ff_8_q);
  and and_27 (and_27_out, not_9_out, not_10_out, not_11_out, not_12_out, d_ff_5_q, not_14_out, d_ff_7_q, not_16_out);
  and and_28 (and_28_out, not_9_out, not_10_out, not_11_out, not_12_out, d_ff_5_q, not_14_out, d_ff_7_q, d_ff_8_q);
  and and_29 (and_29_out, not_9_out, not_10_out, not_11_out, not_12_out, d_ff_5_q, d_ff_6_q, not_15_out, not_16_out);
  and and_30 (and_30_out, not_9_out, not_10_out, not_11_out, not_12_out, d_ff_5_q, d_ff_6_q, not_15_out, d_ff_8_q);
  and and_31 (and_31_out, not_9_out, not_10_out, not_11_out, not_12_out, d_ff_5_q, d_ff_6_q, d_ff_7_q, not_16_out);
  and and_32 (and_32_out, not_9_out, not_10_out, not_11_out, not_12_out, d_ff_5_q, d_ff_6_q, d_ff_7_q, d_ff_8_q);
  or or_7 (or_7_out, and_32_out, and_30_out, and_29_out, and_27_out, and_26_out, and_25_out, and_24_out, and_23_out, and_22_out, and_20_out, and_19_out, and_17_out);
  or or_8 (or_8_out, and_31_out, and_30_out, and_29_out, and_27_out, and_26_out, and_25_out, and_24_out, and_21_out, and_20_out, and_19_out, and_17_out);
  or or_9 (or_9_out, and_32_out, and_31_out, and_30_out, and_27_out, and_26_out, and_25_out, and_24_out, and_23_out, and_22_out, and_21_out, and_20_out, and_17_out);
  Seven_Seg seven_seg_2 (
    .a(or_7_out), .b(or_8_out), .c(or_9_out), .d(or_10_out), .e(or_11_out), .f(or_12_out), .g(or_13_out),
    .dp(1'b0));
  or or_10 (or_10_out, and_32_out, and_30_out, and_29_out, and_27_out, and_26_out, and_25_out, and_23_out, and_22_out, and_20_out, and_19_out, and_17_out);
  or or_11 (or_11_out, and_29_out, and_28_out, and_27_out, and_25_out, and_23_out, and_19_out, and_18_out, and_17_out);
  or or_12 (or_12_out, and_32_out, and_31_out, and_28_out, and_27_out, and_26_out, and_25_out, and_23_out, and_22_out, and_21_out, and_18_out, and_17_out);
  or or_13 (or_13_out, and_32_out, and_31_out, and_30_out, and_29_out, and_26_out, and_25_out, and_23_out, and_22_out, and_21_out, and_20_out, and_19_out);
endmodule
