// Digital circuit Experiment.dig as structural Verilog
module Experiment (
  input  CLK,
  input  Reset,
  input  D,
  output Q,
  output Q_2
);

  wire and_1_out, and_2_out, and_3_out, and_4_out, and_5_out, nor_1_out, nor_2_out, not_1_out, not_2_out,
       not_3_out, or_1_out;

  not not_1 (not_1_out, CLK);
  not not_2 (not_2_out, D);
  and and_1 (and_1_out, not_1_out, not_2_out);
  and and_2 (and_2_out, not_1_out, D);
  not not_3 (not_3_out, Reset);
  and and_3 (and_3_out, and_2_out, not_3_out);
  nor nor_1 (nor_1_out, and_1_out, nor_2_out);
  nor nor_2 (nor_2_out, nor_1_out, and_3_out);
  and and_4 (and_4_out, CLK, nor_2_out);
  and and_5 (and_5_out, CLK, nor_1_out);
  or or_1 (or_1_out, Reset, and_4_out);
  nor nor_3 (Q_2, or_1_out, Q);
  nor nor_4 (Q, Q_2, and_5_out);
endmodule
