// Digital circuit Instruction_register_(IR).dig as structural Verilog
module Instruction_register__IR (
  input  in_1,
  input  in_2,
  input  in_3,
  input  in_4,
  input  in_5,
  input  in_6,
  input  in_7,
  input  in_8,
  input  INSTRUCTION_IN,
  input  INSTRUCTION_OUT,
  output out_11,
  output out_12,
  output out_13,
  output out_14,
  output out_15,
  output out_16,
  output out_17,
  output out_18
);

  wire d_ff_1_q, d_ff_2_q, d_ff_3_q, d_ff_4_q, d_ff_5_q, d_ff_6_q, d_ff_7_q, d_ff_8_q;

  D_FF d_ff_1 (.D(in_1), .C(INSTRUCTION_IN), .Q(d_ff_1_q));  // open: nQ
  D_FF d_ff_2 (.D(in_2), .C(INSTRUCTION_IN), .Q(d_ff_2_q));  // open: nQ
  assign out_11 = INSTRUCTION_OUT ? d_ff_1_q : 1'bz;  // Driver driver_1
  assign out_12 = INSTRUCTION_OUT ? d_ff_2_q : 1'bz;  // Driver driver_2
  D_FF d_ff_3 (.D(in_3), .C(INSTRUCTION_IN), .Q(d_ff_3_q));  // open: nQ
  D_FF d_ff_4 (.D(in_4), .C(INSTRUCTION_IN), .Q(d_ff_4_q));  // open: nQ
  assign out_13 = INSTRUCTION_OUT ? d_ff_3_q : 1'bz;  // Driver driver_3
  assign out_14 = INSTRUCTION_OUT ? d_ff_4_q : 1'bz;  // Driver driver_4
  D_FF d_ff_5 (.D(in_5), .C(INSTRUCTION_IN), .Q(d_ff_5_q));  // open: nQ
  D_FF d_ff_6 (.D(in_6), .C(INSTRUCTION_IN), .Q(d_ff_6_q));  // open: nQ
  assign out_15 = INSTRUCTION_OUT ? d_ff_5_q : 1'bz;  // Driver driver_5
  assign out_16 = INSTRUCTION_OUT ? d_ff_6_q : 1'bz;  // Driver driver_6
  D_FF d_ff_7 (.D(in_7), .C(INSTRUCTION_IN), .Q(d_ff_7_q));  // open: nQ
  D_FF d_ff_8 (.D(in_8), .C(INSTRUCTION_IN), .Q(d_ff_8_q));  // open: nQ
  assign out_17 = INSTRUCTION_OUT ? d_ff_7_q : 1'bz;  // Driver driver_7
  assign out_18 = INSTRUCTION_OUT ? d_ff_8_q : 1'bz;  // Driver driver_8
endmodule
