// Digital circuit Memory_address_register_(MAR).dig as structural Verilog
module Memory_address_register__MAR (
  input  BIT_1,
  input  BIT_2,
  input  BIT_3,
  input  BIT_4,
  input  MAR_IN,
  output out_6,
  output out_7,
  output out_8,
  output out_9
);

  D_FF d_ff_1 (.D(BIT_1), .C(MAR_IN), .Q(out_8));  // open: nQ
  D_FF d_ff_2 (.D(BIT_2), .C(MAR_IN), .Q(out_7));  // open: nQ
  D_FF d_ff_3 (.D(BIT_3), .C(MAR_IN), .Q(out_6));  // open: nQ
  D_FF d_ff_4 (.D(BIT_4), .C(MAR_IN), .Q(out_9));  // open: nQ
endmodule
