// Digital circuit Step_Counter_(SC).dig as structural Verilog
module Step_Counter__SC (
  input  Add,
  input  PC_OUT
);

  wire add_1_c_o, add_1_s, add_2_c_o, add_2_s, add_3_c_o, add_3_s, and_1_out, and_2_out, and_3_out,
       and_4_out, and_5_out, and_6_out, d_ff_1_q, d_ff_2_q, d_ff_3_q, not_1_out, not_2_out, not_3_out,
       or_1_out, or_2_out, or_3_out;

  Add add_1 (.a(d_ff_1_q), .b(1'b0), .c_i(add_2_c_o), .s(add_1_s), .c_o(add_1_c_o));
  Add add_2 (.a(d_ff_2_q), .b(1'b0), .c_i(add_3_c_o), .s(add_2_s), .c_o(add_2_c_o));
  Add add_3 (.a(d_ff_3_q), .b(1'b1), .c_i(Add), .s(add_3_s), .c_o(add_3_c_o));
  not not_1 (not_1_out, d_ff_1_q);
  and and_1 (and_1_out, not_1_out, add_1_s);
  or or_1 (or_1_out, and_2_out, and_1_out);
  and and_2 (and_2_out, 1'b0, d_ff_1_q);
  not not_2 (not_2_out, d_ff_1_q);
  and and_3 (and_3_out, not_2_out, add_2_s);
  D_FF d_ff_1 (.D(or_1_out), .C(PC_OUT), .Q(d_ff_1_q));  // open: nQ
  or or_2 (or_2_out, and_4_out, and_3_out);
  D_FF d_ff_2 (.D(or_2_out), .C(PC_OUT), .Q(d_ff_2_q));  // open: nQ
  and and_4 (and_4_out, 1'b0, d_ff_1_q);
  D_FF d_ff_3 (.D(or_3_out), .C(PC_OUT), .Q(d_ff_3_q));  // open: nQ
  not not_3 (not_3_out, d_ff_1_q);
  and and_5 (and_5_out, not_3_out, add_3_s);
  or or_3 (or_3_out, and_6_out, and_5_out);
  and and_6 (and_6_out, 1'b0, d_ff_1_q);
endmodule
