// Digital circuit program_counter_(PC).dig as structural Verilog
module program_counter__PC (
  input  Add,
  input  PC_OUT,
  input  in_3,
  input  in_4,
  input  in_5,
  input  in_6,
  input  PC_IN
);

  wire add_1_c_o, add_1_s, add_2_c_o, add_2_s, add_3_c_o, add_3_s, add_4_c_o, add_4_s, and_1_out, and_2_out,
       and_3_out, and_4_out, and_5_out, and_6_out, and_7_out, and_8_out, d_ff_1_q, d_ff_2_q, d_ff_3_q,
       d_ff_4_q, not_1_out, not_2_out, not_3_out, not_4_out, or_1_out, or_2_out, or_3_out, or_4_out;

  Add add_1 (.a(d_ff_1_q), .b(1'b0), .c_i(add_2_c_o), .s(add_1_s), .c_o(add_1_c_o));
  Add add_2 (.a(d_ff_2_q), .b(1'b0), .c_i(add_3_c_o), .s(add_2_s), .c_o(add_2_c_o));
  Add add_3 (.a(d_ff_3_q), .b(1'b0), .c_i(add_4_c_o), .s(add_3_s), .c_o(add_3_c_o));
  Add add_4 (.a(d_ff_4_q), .b(1'b1), .c_i(Add), .s(add_4_s), .c_o(add_4_c_o));
  not not_1 (not_1_out, PC_IN);
  and and_1 (and_1_out, not_1_out, add_1_s);
  or or_1 (or_1_out, and_2_out, and_1_out);
  and and_2 (and_2_out, in_3, PC_IN);
  not not_2 (not_2_out, PC_IN);
  and and_3 (and_3_out, not_2_out, add_2_s);
  D_FF d_ff_1 (.D(or_1_out), .C(PC_OUT), .Q(d_ff_1_q));  // open: nQ
  or or_2 (or_2_out, and_4_out, and_3_out);
  D_FF d_ff_2 (.D(or_2_out), .C(PC_OUT), .Q(d_ff_2_q));  // open: nQ
  and and_4 (and_4_out, in_4, PC_IN);
  not not_3 (not_3_out, PC_IN);
  and and_5 (and_5_out, not_3_out, add_3_s);
  D_FF d_ff_3 (.D(or_3_out), .C(PC_OUT), .Q(d_ff_3_q));  // open: nQ
  D_FF d_ff_4 (.D(or_4_out), .C(PC_OUT), .Q(d_ff_4_q));  // open: nQ
  or or_3 (or_3_out, and_6_out, and_5_out);
  and and_6 (and_6_out, in_5, PC_IN);
  not not_4 (not_4_out, PC_IN);
  and and_7 (and_7_out, not_4_out, add_4_s);
  or or_4 (or_4_out, and_8_out, and_7_out);
  and and_8 (and_8_out, in_6, PC_IN);
endmodule
