// Digital circuit tristate_buffer.dig as structural Verilog
module tristate_buffer (
  input  A,
  input  Enable,
  output Y
);

  wire not_1_out;

  FGPFET fgpfet_1 (.G(not_1_out), .S(A), .D(Y));
  FGNFET fgnfet_1 (.G(Enable), .D(A), .S(Y));
  not not_1 (not_1_out, Enable);

  // Notes on the sheet:
  //   A: Input
  //   Enable: Control line
endmodule
